// Logisim project Circuito de entradas de dados.circ as structural Verilog: 6 circuits, main circuit main
module main (
);

  Somador7bts somador7bts_1 ();  // open: Ci, A0, B0, A1, B1, A2, B2, A3, B3, A4, B4, A5, B5, A6, B6, S0, S1, S2, S3, S4, S5, S6, Cout
endmodule

module Somador1bt (
  input  Ci,
  input  A,
  input  B,
  output S,
  output Co
);

  wire and_1_out, and_2_out, and_3_out, xor_1_out;

  xor xor_1 (xor_1_out, B, Ci);
  and and_1 (and_1_out, A, B);
  and and_2 (and_2_out, A, Ci);
  and and_3 (and_3_out, B, Ci);
  xor xor_2 (S, A, xor_1_out);
  or or_1 (Co, and_1_out, and_2_out, and_3_out);
endmodule

module Botoes (
  input  A,
  input  B,
  input  C,
  input  Ch0,
  output N0,
  output N1,
  output out_7
);

  wire not_1_out, not_2_out, xor_1_out, xor_2_out;

  xor xor_1 (xor_1_out, A, B);
  not not_1 (not_1_out, C);
  not not_2 (not_2_out, B);
  xor xor_2 (xor_2_out, A, C);
  and and_1 (N0, xor_1_out, not_1_out);
  and and_2 (N1, not_2_out, xor_2_out);

  assign out_7 = Ch0;
endmodule

module Somador7bts (
  input  Ci,
  input  A0,
  input  B0,
  input  A1,
  input  B1,
  input  A2,
  input  B2,
  input  A3,
  input  B3,
  input  A4,
  input  B4,
  input  A5,
  input  B5,
  input  A6,
  input  B6,
  output S0,
  output S1,
  output S2,
  output S3,
  output S4,
  output S5,
  output S6,
  output Cout
);

  wire somador1bt_1_co, somador1bt_2_co, somador1bt_3_co, somador1bt_4_co, somador1bt_5_co, somador1bt_6_co;

  Somador1bt somador1bt_1 (.Ci(Ci), .A(A0), .B(B0), .S(S0), .Co(somador1bt_1_co));
  Somador1bt somador1bt_2 (.Ci(somador1bt_1_co), .A(A1), .B(B1), .S(S1), .Co(somador1bt_2_co));
  Somador1bt somador1bt_3 (.Ci(somador1bt_2_co), .A(A2), .B(B2), .S(S2), .Co(somador1bt_3_co));
  Somador1bt somador1bt_4 (.Ci(somador1bt_3_co), .A(A3), .B(B3), .S(S3), .Co(somador1bt_4_co));
  Somador1bt somador1bt_5 (.Ci(somador1bt_4_co), .A(A4), .B(B4), .S(S4), .Co(somador1bt_5_co));
  Somador1bt somador1bt_6 (.Ci(somador1bt_5_co), .A(A5), .B(B5), .S(S5), .Co(somador1bt_6_co));
  Somador1bt somador1bt_7 (.Ci(somador1bt_6_co), .A(A6), .B(B6), .S(S6), .Co(Cout));
endmodule

module Somador_Subtrator (
  input  Ci,
  input  A0,
  input  B0,
  input  A1,
  input  B1,
  input  A2,
  input  B2,
  input  A3,
  input  B3,
  input  A4,
  input  B4,
  input  A5,
  input  B5,
  input  A6,
  input  B6,
  output S0,
  output S1,
  output S2,
  output S3,
  output S4,
  output S5,
  output S6,
  output Cout
);

  wire xor_1_out, xor_2_out, xor_3_out, xor_4_out, xor_5_out, xor_6_out, xor_7_out;

  xor xor_1 (xor_1_out, B0, Ci);
  xor xor_2 (xor_2_out, B1, Ci);
  xor xor_3 (xor_3_out, B2, Ci);
  xor xor_4 (xor_4_out, B3, Ci);
  xor xor_5 (xor_5_out, B4, Ci);
  xor xor_6 (xor_6_out, B5, Ci);
  xor xor_7 (xor_7_out, B6, Ci);
  Somador7bts somador7bts_1 (
    .Ci(Ci), .A0(A0), .B0(xor_1_out), .A1(A1), .B1(xor_2_out), .A2(A2), .B2(xor_3_out), .A3(A3),
    .B3(xor_4_out), .A4(A4), .B4(xor_5_out), .A5(A5), .B5(xor_6_out), .A6(A6), .B6(xor_7_out), .S0(S0),
    .S1(S1), .S2(S2), .S3(S3), .S4(S4), .S5(S5), .S6(S6), .Cout(Cout));
endmodule

module Entradas_e_Somas (
  input  Bt2,
  input  Bt1,
  input  Bt0,
  input  Chave,
  input  A0,
  input  A1,
  input  A2,
  input  B2,
  input  A3,
  input  B3,
  input  A4,
  input  B4,
  input  A5,
  input  B5,
  input  A6,
  input  B6,
  output S0,
  output S1,
  output S2,
  output S3,
  output S4,
  output S5,
  output S6,
  output Cout
);

  wire botoes_1_n0, botoes_1_n1, botoes_1_out_7;

  Botoes botoes_1 (.A(Bt2), .B(Bt1), .C(Bt0), .Ch0(Chave), .N0(botoes_1_n0), .N1(botoes_1_n1), .out_7(botoes_1_out_7));
  Somador_Subtrator somador_subtrator_1 (
    .Ci(botoes_1_out_7), .A0(A0), .B0(botoes_1_n0), .A1(A1), .B1(botoes_1_n1), .A2(A2), .B2(B2), .A3(A3),
    .B3(B3), .A4(A4), .B4(B4), .A5(A5), .B5(B5), .A6(A6), .B6(B6), .S0(S0), .S1(S1), .S2(S2), .S3(S3),
    .S4(S4), .S5(S5), .S6(S6), .Cout(Cout));

  // Notes on the sheet:
  //   N3
  //   N1
  //   N2
endmodule
